# Fritzing sketch circuit (saved by Fritzing 0.9.3b)
breadboards: 1

parts:
  Componente1 = Arduino Uno (Rev3) - ICSP
  Componente4 = NRF24L01+ Breakout Board
  S2 = Momentary Switch [package=ksa_sealed_tac_switch]
  LED1 = smd LED [color="Red (633nm)" package="0805 [SMD]"]
  R1 = Resistor [tolerance=±5% resistance=220 package="0402 [SMD]"]
  Componente5 = Arduino Uno (Rev3) - ICSP
  Componente6 = NRF24L01+ Breakout Board
  LED2 = smd LED [color="Red (633nm)" package="0805 [SMD]"]
  S3 = Pushbutton [package="[THT]"]
  R2 = Resistor [tolerance=±5% resistance=220 package="0402 [SMD]"]

nets:
  N1: Componente1.A0, S2.3
  GND: Componente1.A1, Componente1.GND, Componente4.GND, S2.4, LED1.cathode, S3.Pin_3, S3.Pin_4
  N2: Componente1.D8, Componente4.CE
  N3: Componente1.D11_PWM/MOSI, Componente4.MOSI
  N4: Componente1.D12/MISO, Componente4.MISO
  N5: Componente1.D13/SCK, Componente4.SCK
  N6: Componente1.D2, Componente4.IRQ
  N7: Componente1.D4, LED1.anode
  N8: Componente1.D7, Componente4.CS
  3V3: Componente1.3V3, Componente4.VCC
  N9: Componente1.5V, R1.Pin_1, R2.Pin_1
  N10: S2.2, R1.Pin_0
  N11: Componente5.D8, Componente6.CE
  N12: Componente5.D11_PWM/MOSI, Componente6.MOSI
  N13: Componente5.D12/MISO, Componente6.MISO
  N14: Componente5.D13/SCK, Componente6.SCK
  GND_2: Componente5.GND, Componente6.GND, LED2.cathode
  N15: Componente5.D2, Componente6.IRQ
  N16: Componente5.D4, LED2.anode
  N17: Componente5.D7, Componente6.CS
  3V3_2: Componente5.3V3, Componente6.VCC
  N18: S3.Pin_1, S3.Pin_2, R2.Pin_0
